// Digital circuit ALU.dig as structural Verilog
module ALU (
  input  [3:0] A,
  input  [2:0] S1_S0_Cin,
  input  [3:0] B,
  output Overflow,
  output [3:0] D
);

  wire [3:0] _4_bit_adder_modified_1_p2, not_1_out, not_2_out;

  assign not_1_out = ~4'b0000;  // Not not_1, 4 bits wide
  assign not_2_out = ~B;  // Not not_2, 4 bits wide
  // _4_bit_adder_modified _4_bit_adder_modified_1: pin names not known; wires that end beside it: A, _4_bit_adder_modified_1_p2, S1_S0_Cin[0], D, Overflow
  Multiplexer #(.Selector_Bits(2), .Bits(4)) multiplexer_1 (
    .sel(S1_S0_Cin[2:1]), .in_0(B), .in_1(not_2_out), .in_2(4'b0000), .in_3(not_1_out),
    .out(_4_bit_adder_modified_1_p2));
endmodule
