// Digital circuit registers-file.dig as structural Verilog
module registers_file (
  input  [1:0] Select_read1,
  input  [1:0] Select_read2,
  input  Clock,
  input  [3:0] Write_data,
  input  [1:0] Select_Write,
  input  [7:0] ctrl_registers,
  output [3:0] Read_data_1,
  output [3:0] Read_data_2
);

  wire [3:0] demultiplexer_1_out_0, demultiplexer_1_out_1, demultiplexer_1_out_2, demultiplexer_1_out_3,
       R_0_p4, R_1_p4, R_2_p4, R_3_p4;

  Demultiplexer #(.Selector_Bits(2), .Bits(4)) demultiplexer_1 (
    .sel(Select_Write), .in(Write_data), .out_0(demultiplexer_1_out_0), .out_1(demultiplexer_1_out_1),
    .out_2(demultiplexer_1_out_2), .out_3(demultiplexer_1_out_3));
  // _4_bit_register R_0: pin names not known; wires that end beside it: demultiplexer_1_out_0, ctrl_registers[1:0], Clock, R_0_p4
  // _4_bit_register R_1: pin names not known; wires that end beside it: demultiplexer_1_out_1, ctrl_registers[3:2], Clock, R_1_p4
  // _4_bit_register R_2: pin names not known; wires that end beside it: demultiplexer_1_out_2, ctrl_registers[5:4], Clock, R_2_p4
  // _4_bit_register R_3: pin names not known; wires that end beside it: demultiplexer_1_out_3, ctrl_registers[7:6], Clock, R_3_p4
  Multiplexer #(.Selector_Bits(2), .Bits(4)) multiplexer_1 (
    .sel(Select_read1), .in_0(R_0_p4), .in_1(R_1_p4), .in_2(R_2_p4), .in_3(R_3_p4), .out(Read_data_1));
  Multiplexer #(.Selector_Bits(2), .Bits(4)) multiplexer_2 (
    .sel(Select_read2), .in_0(R_0_p4), .in_1(R_1_p4), .in_2(R_2_p4), .in_3(R_3_p4), .out(Read_data_2));
endmodule
